// Logisim project group13projectcse332.circ as structural Verilog: 7 circuits, main circuit main
module main (
  input  [2:0] write_register,
  input  [14:0] Write_data,
  input  enable_write_control,
  input  CLOCK,
  input  clear,
  input  [2:0] Read_register_1,
  input  [2:0] Read_register_2,
  output [14:0] read_data_2,
  output [14:0] read_data_1
);

  wire and_1_out, and_2_out, and_3_out, and_4_out, and_5_out, and_6_out, and_7_out, and_8_out,
       decoder_1_out0, decoder_1_out1, decoder_1_out2, decoder_1_out3, decoder_1_out4, decoder_1_out5,
       decoder_1_out6, decoder_1_out7;
  wire [14:0] R0_q, R1_q, R2_q, R3_q, R4_q, R5_q, R6_q, R7_q;

  Decoder #(.select(3)) decoder_1 (
    .out0(decoder_1_out0), .out1(decoder_1_out1), .out2(decoder_1_out2), .out3(decoder_1_out3),
    .out4(decoder_1_out4), .out5(decoder_1_out5), .out6(decoder_1_out6), .out7(decoder_1_out7),
    .sel(write_register));  // open: en
  and and_1 (and_1_out, decoder_1_out0, enable_write_control);
  and and_2 (and_2_out, decoder_1_out1, enable_write_control);
  and and_3 (and_3_out, decoder_1_out2, enable_write_control);
  and and_4 (and_4_out, decoder_1_out3, enable_write_control);
  and and_5 (and_5_out, decoder_1_out4, enable_write_control);
  and and_6 (and_6_out, decoder_1_out5, enable_write_control);
  and and_7 (and_7_out, decoder_1_out6, enable_write_control);
  and and_8 (and_8_out, decoder_1_out7, enable_write_control);
  Register #(.width(15)) R0 (.D(Write_data), .en(and_1_out), .Q(R0_q), .clk(CLOCK), .clr(clear));
  Register #(.width(15)) R1 (.D(Write_data), .en(and_2_out), .Q(R1_q), .clk(CLOCK), .clr(clear));
  Register #(.width(15)) R2 (.D(Write_data), .en(and_3_out), .Q(R2_q), .clk(CLOCK), .clr(clear));
  Register #(.width(15)) R3 (.D(Write_data), .en(and_4_out), .Q(R3_q), .clk(CLOCK), .clr(clear));
  Register #(.width(15)) R4 (.D(Write_data), .en(and_5_out), .Q(R4_q), .clk(CLOCK), .clr(clear));
  Register #(.width(15)) R5 (.D(Write_data), .en(and_6_out), .Q(R5_q), .clk(CLOCK), .clr(clear));
  Register #(.width(15)) R6 (.D(Write_data), .en(and_7_out), .Q(R6_q), .clk(CLOCK), .clr(clear));
  Register #(.width(15)) R7 (.D(Write_data), .en(and_8_out), .Q(R7_q), .clk(CLOCK), .clr(clear));
  Multiplexer #(.select(3), .width(15)) multiplexer_1 (
    .in0(R0_q), .in1(R1_q), .in2(R2_q), .in3(R3_q), .in4(R4_q), .in5(R5_q), .in6(R6_q), .in7(R7_q),
    .out(read_data_1), .sel(Read_register_1));  // open: en
  Multiplexer #(.select(3), .width(15)) multiplexer_2 (
    .in0(R0_q), .in1(R1_q), .in2(R2_q), .in3(R3_q), .in4(R4_q), .in5(R5_q), .in6(R6_q), .in7(R7_q),
    .out(read_data_2), .sel(Read_register_2));  // open: en

  // Notes on the sheet:
  //   15 bits Register File
  //                                              Name Shefa Tabassum   ID: 2232993042 
  //   Easfiah Hossain Lamia ID 2231699642
endmodule

module Control_Unit (
  input  [2:0] opcode,
  output [1:0] ALU_OP,
  output Reg_Dest,
  output ALU_src,
  output MemToReg,
  output WC_RegWrite,
  output Load_Memory_read,
  output branch,
  output Mem_Enable_MemWrite_sw,
  output jump
);

  wire decoder_1_out2, decoder_1_out3, decoder_1_out7;

  Decoder #(.select(3)) decoder_1 (
    .out0(Reg_Dest), .out1(branch), .out2(decoder_1_out2), .out3(decoder_1_out3),
    .out4(Mem_Enable_MemWrite_sw), .out5(jump), .out6(Load_Memory_read), .out7(decoder_1_out7), .sel(opcode));  // open: en
  or or_1 (ALU_src, decoder_1_out3, decoder_1_out2, Mem_Enable_MemWrite_sw, Load_Memory_read);
  or or_2 (ALU_OP[0], Mem_Enable_MemWrite_sw, decoder_1_out2, Load_Memory_read, decoder_1_out3);
  or or_3 (ALU_OP[1], Reg_Dest, decoder_1_out2);
  or or_4 (WC_RegWrite, decoder_1_out2, decoder_1_out3, Reg_Dest, Load_Memory_read);

  assign MemToReg = Load_Memory_read;

  // Notes on the sheet:
  //   ori 010
  //   addi 011
  //   sw 100
  //   beq 001
  //   lw 110
  //    Name Shefa Tabassum   ID: 2232993042 
  //   Easfiah Hossain Lamia ID 2231699642
  //   ori
  //   for r type
  //   ori
  //   sw
  //   lw
  //   lw
  //   ori
  //   addi
  //   lw
  //   lw
  //   beq
  //   sw
  //   jmp
  //   Control Unit
endmodule

module ALU_control (
  input  [1:0] ALUOP,
  input  [2:0] FUNC,
  output AND,
  output PIN_0,
  output PIN_1,
  output PIN_2
);

  wire and_2_out, and_3_out, decoder_1_out0, decoder_1_out1, decoder_1_out2, decoder_1_out3, decoder_1_out4,
       decoder_1_out5, decoder_1_out6, decoder_1_out7, decoder_2_out0, decoder_2_out1, decoder_2_out2,
       or_2_out;

  Decoder #(.select(3), .enable("false")) decoder_1 (
    .out0(decoder_1_out0), .out1(decoder_1_out1), .out2(decoder_1_out2), .out3(decoder_1_out3),
    .out4(decoder_1_out4), .out5(decoder_1_out5), .out6(decoder_1_out6), .out7(decoder_1_out7), .sel(FUNC));
  Decoder #(.select(2), .enable("false")) decoder_2 (
    .out0(decoder_2_out0), .out1(decoder_2_out1), .out2(decoder_2_out2), .out3(PIN_2), .sel(ALUOP));
  and and_1 (AND, decoder_1_out0, decoder_2_out2);
  and and_2 (and_2_out, decoder_1_out1, decoder_2_out2);
  and and_3 (and_3_out, decoder_1_out2, decoder_2_out2);
  or or_1 (PIN_0, decoder_2_out1, and_2_out);
  or or_2 (or_2_out, decoder_2_out0, and_3_out);
  or or_3 (PIN_1, decoder_2_out1, or_2_out);

  // Notes on the sheet:
  //   000 nop
  //   001 xor
  //   000 and
  //   010 sub
  //   xor
  //   beq
  //   sub
  //   ALU Control
  //   addi/sw/lw
  //   ori
  //                                              Name Shefa Tabassum   ID: 2232993042 
  //   Easfiah Hossain Lamia ID 2231699642
endmodule

module ALU (
  input  [14:0] A,
  input  [14:0] B,
  input  [1:0] ALU_OP,
  input  [2:0] func,
  output [14:0] \output ,
  output zero,
  output overflow
);

  wire adder_1_cout, adder_2_cout, not_2_out;
  wire [2:0] alu_control_1_pin_0;
  wire [14:0] adder_1_out, adder_2_out, and_1_out, not_1_out, or_1_out, xor_1_out;

  assign not_1_out = ~B;  // NOT_Gate not_1, 15 bits wide
  assign or_1_out = A | B;  // OR_Gate or_1, 15 bits wide
  Adder #(.width(15)) adder_1 (.a(A), .b(B), .out(adder_1_out), .cin(1'b0), .cout(adder_1_cout));
  Adder #(.width(15)) adder_2 (.a(A), .b(not_1_out), .out(adder_2_out), .cin(1'b1), .cout(adder_2_cout));
  assign and_1_out = A & B;  // AND_Gate and_1, 15 bits wide
  assign xor_1_out = A ^ B;  // XOR_Gate xor_1, 15 bits wide
  not not_2 (not_2_out, adder_2_cout);
  ALU_control alu_control_1 (
    .FUNC(func), .ALUOP(ALU_OP), .PIN_2(alu_control_1_pin_0[2]), .PIN_1(alu_control_1_pin_0[1]),
    .PIN_0(alu_control_1_pin_0[0]));  // open: AND
  Multiplexer #(.select(3), .width(15), .enable("false")) multiplexer_1 (
    .in0(and_1_out), .in1(xor_1_out), .in2(adder_2_out), .in3(adder_1_out), .in4(or_1_out), .out(\output ),
    .sel(alu_control_1_pin_0));  // open: in5, in6, in7
  nor nor_1 (zero, \output [0], \output [1], \output [2], \output [3], \output [4], \output [5], \output [6], \output [7], \output [8], \output [9], \output [10], \output [11], \output [12], \output [13], \output [14]);
  Multiplexer #(.select(3)) multiplexer_2 (
    .in0(1'b0), .in1(1'b0), .in2(not_2_out), .in3(adder_1_cout), .in4(1'b0), .in5(1'b0), .in6(1'b0),
    .in7(1'b0), .out(overflow), .sel(alu_control_1_pin_0));  // open: en

  // Notes on the sheet:
  //   or
  //   ADD
  //   add overflow
  //   SUB
  //   AND
  //   xor
  //   sub overflow
  //   Arithmetic Logic Unit
  //                                              Name Shefa Tabassum   ID: 2232993042 
  //   Easfiah Hossain Lamia ID 2231699642
endmodule

module datapath (
  output [14:0] out_1,
  output [14:0] out_2,
  output [14:0] out_3,
  output [14:0] out_4,
  output [2:0] out_5,
  output [2:0] out_6,
  output [14:0] out_7,
  output [14:0] out_8,
  output [14:0] out_9,
  output [2:0] out_10,
  output [14:0] out_11,
  output [2:0] out_12,
  output [2:0] out_13,
  output [14:0] ALUsrc,
  output overflow,
  output [2:0] ori_010,
  output [14:0] out_17,
  output [14:0] out_18,
  output [14:0] out_19,
  output [14:0] out_20,
  output [1:0] out_21
);

  wire alu_1_zero, and_1_out, and_2_out, and_3_out, clk_out, control_unit_1_alu_src, control_unit_1_branch,
       control_unit_1_jump, control_unit_1_load_memory_read, control_unit_1_mem_enable_memwrite_sw,
       control_unit_1_memtoreg, control_unit_1_reg_dest, control_unit_1_wc_regwrite, nop_1_result,
       reset_2_out, reset_out;
  wire [14:0] adder_1_out, ram_1_data;

  Hex_Digit_Display hex_digit_display_1 (.value({1'b0, out_11[14:12]}));  // open: dp
  Hex_Digit_Display hex_digit_display_2 (.value(out_11[11:8]));  // open: dp
  NOP nop_1 (.in_1({ori_010, out_13, out_12, out_10, out_5}), .Result(nop_1_result));
  PC pc_1 (.PCin(out_1), .PCout(out_17), .clk(clk_out), .reset(reset_out));
  Hex_Digit_Display hex_digit_display_3 (.value(out_11[3:0]));  // open: dp
  Hex_Digit_Display hex_digit_display_4 (.value(out_11[7:4]));  // open: dp
  Adder #(.width(15)) adder_1 (.a(15'h1), .b(out_17), .out(adder_1_out));  // open: cin, cout
  ROM #(.addrWidth(15), .dataWidth(15)) rom_1 (
    .addr(out_17), .data({ori_010, out_13, out_12, out_10, out_5}));  // open: sel
  Hex_Digit_Display hex_digit_display_5 (.value({1'b0, ori_010}));  // open: dp
  assign out_4 = {{3{1'b0}}, {out_13, out_12, out_10, out_5}};  // Bit_Extender bit_extender_1
  Hex_Digit_Display hex_digit_display_6 (.value({out_13, out_12[2]}));  // open: dp
  Hex_Digit_Display hex_digit_display_7 (.value({out_12[1:0], out_10[2:1]}));  // open: dp
  Hex_Digit_Display hex_digit_display_8 (.value({out_10[0], out_5}));  // open: dp
  Multiplexer #(.width(3), .enable("false")) multiplexer_1 (
    .in0(out_12), .in1(out_10), .out(out_6), .sel(control_unit_1_reg_dest));
  and and_1 (and_1_out, ~nop_1_result, control_unit_1_wc_regwrite);  // AND_Gate
  assign out_2 = {{9{1'b0}}, {out_10, out_5}};  // Bit_Extender bit_extender_2
  Button reset (.out(reset_out));
  main main_1 (
    .write_register(out_6), .Write_data(out_11), .enable_write_control(and_1_out), .CLOCK(clk_out),
    .clear(reset_out), .Read_register_1(out_13), .Read_register_2(out_12), .read_data_2(out_7),
    .read_data_1(out_8));
  Clock clk (.out(clk_out));
  Multiplexer #(.width(15), .enable("false")) multiplexer_2 (
    .in0(out_7), .in1(out_2), .out(ALUsrc), .sel(control_unit_1_alu_src));
  Control_Unit control_unit_1 (
    .opcode(ori_010), .ALU_OP(out_21), .Reg_Dest(control_unit_1_reg_dest), .ALU_src(control_unit_1_alu_src),
    .MemToReg(control_unit_1_memtoreg), .WC_RegWrite(control_unit_1_wc_regwrite),
    .Load_Memory_read(control_unit_1_load_memory_read), .branch(control_unit_1_branch),
    .Mem_Enable_MemWrite_sw(control_unit_1_mem_enable_memwrite_sw), .jump(control_unit_1_jump));
  ALU alu_1 (
    .func(out_5), .\output (out_9), .zero(alu_1_zero), .A(out_8), .B(ALUsrc), .ALU_OP(out_21),
    .overflow(overflow));
  and and_2 (and_2_out, alu_1_zero, control_unit_1_branch);
  and and_3 (and_3_out, ~nop_1_result, 1'b1);  // AND_Gate
  Multiplexer #(.width(15), .enable("false")) multiplexer_3 (
    .in0(adder_1_out), .in1(out_2), .out(out_3), .sel(and_2_out));
  RAM #(.addrWidth(15), .dataWidth(15), .bus("separate")) ram_1 (
    .addr(out_9), .din(out_7), .data(ram_1_data), .str(control_unit_1_mem_enable_memwrite_sw),
    .sel(and_3_out), .clk(clk_out), .ld(control_unit_1_load_memory_read), .clr(reset_2_out));
  Button reset_2 (.out(reset_2_out));
  Multiplexer #(.width(15), .enable("false")) multiplexer_4 (
    .in0(out_9), .in1(ram_1_data), .out(out_11), .sel(control_unit_1_memtoreg));
  Multiplexer #(.width(15), .enable("false")) multiplexer_5 (
    .in0(out_3), .in1(out_4), .out(out_1), .sel(control_unit_1_jump));

  assign out_18 = out_7;
  assign out_19 = out_1;
  assign out_20 = {ori_010, out_13, out_12, out_10, out_5};

  // Notes on the sheet:
  //   Write Data
  //   NOP
  //   stop
  //   contents of rom_1 (hex, n*v repeats v):
  //   3045 3086 1445 29a 5006 298
  //   ROM
  //                                              Name Shefa Tabassum   ID: 2232993042 
  //   jump address
  //   Easfiah Hossain Lamia ID 2231699642
  //   000 nop
  //   000 and
  //   INS DATA
  //   001 xor
  //   010 sub
  //   func
  //   rd
  //   rt
  //   rs
  //   opcode
  //   addi 011
  //   sw 100
  //   beq 001
  //   lw 110
  //   jmp 101
  //   Fig: Datapath
  //   stop
  //   immediate
  //   zero flag
  //   branch adrress
  //   beq
  //   stop
  //   jmp address
  //   RAM
  //   to pcin
  //   jmp
endmodule

module PC (
  input  [14:0] PCin,
  input  clk,
  input  reset,
  output [14:0] PCout
);

  Register #(.width(15)) register_1 (.D(PCin), .Q(PCout), .clk(clk), .clr(reset));  // open: en

  // Notes on the sheet:
  //                                              Name Shefa Tabassum   ID: 2232993042 
  //   Easfiah Hossain Lamia ID 2231699642
  //   Program Counter
endmodule

module NOP (
  input  [14:0] in_1,
  output Result
);

  Comparator #(.width(15)) comparator_1 (.a(in_1), .b({15{1'b0}}), .eq(Result));  // open: gt, lt

  // Notes on the sheet:
  //                                              Name Shefa Tabassum   ID: 2232993042 
  //   INS
  //   Easfiah Hossain Lamia ID 2231699642
  //   NOP
endmodule
